# Fritzing sketch pltn_range_sensor (saved by Fritzing 0.7.11b)
breadboards: 1

parts:
  Arduino1 = Arduino
  Q4 = Basic FET N-Channel [package="TO220 [THT]"]
  Q5 = Basic FET N-Channel [package="TO220 [THT]"]
  Q6 = Basic FET N-Channel [package="TO220 [THT]"]
  Q7 = Basic FET N-Channel [package="TO220 [THT]"]
  Q8 = Basic FET N-Channel [package="TO220 [THT]"]
  Q9 = Basic FET N-Channel [package="TO220 [THT]"]
  LED2 = Super Flux LED blue [color=Blue]
  LED3 = Super Flux LED blue [color=Green]
  LED4 = Super Flux LED blue [color=Red]
  LED5 = Super Flux LED blue [color=Blue]
  LED6 = Super Flux LED blue [color=Green]
  LED7 = Super Flux LED blue [color=Red]
  J1 = Infrared Proximity Sensor

nets:
  GND: Arduino1.GND, Q4.source, Q5.source, Q6.source, Q7.source, Q8.source, Q9.source, J1.GND
  N1: Arduino1.D11, Q6.gate
  N2: Arduino1.D10, Q5.gate
  N3: Arduino1.D9, Q4.gate
  N4: Arduino1.D6, Q7.gate
  N5: Arduino1.D5, Q9.gate
  N6: Arduino1.D3, Q8.gate
  +5V: Arduino1.+5V, J1.Vcc
  N7: Arduino1.VIN, LED4.cathode, LED7.cathode
  N8: Arduino1.A0, J1.Vout
  N9: Q4.drain, LED5.anode
  N10: Q5.drain, LED7.anode
  N11: Q6.drain, LED6.anode
  N12: Q7.drain, LED3.anode
  N13: Q8.drain, LED4.anode
  N14: Q9.drain, LED2.anode

notes:
  LED 1
  LED 2
  Maxbotix Ultra Range Sensor
  - option A wire Vin to breadboard (does it support 12v??)
  - option B is external 12v female adapter
