# Fritzing sketch LCD (saved by Fritzing 0.7.11b)
breadboards: 1

parts:
  Arduino1 = Arduino
  R1 = Rotary Potentiometer (Large) [maximum_resistance=100kΩ package=THT]
  LCD1 = LCD screen

nets:
  N1: Arduino1.D12, LCD1.RS
  N2: Arduino1.D11, LCD1.E
  N3: Arduino1.D5, LCD1.DB2, LCD1.DB3, LCD1.DB4
  N4: Arduino1.D4, LCD1.DB5
  N5: Arduino1.D3, LCD1.DB6
  N6: Arduino1.D2, LCD1.DB7
  N7: Arduino1.+5V, LCD1.LED+
  N8: Arduino1.GND, R1.leg1, LCD1.LED-
  N9: R1.wiper, LCD1.V0
  N10: R1.leg2, LCD1.VDD
