# Fritzing sketch platoon_RPi (saved by Fritzing 0.7.11b)
breadboards: 1

parts:
  Q4 = Basic FET N-Channel [package="TO220 [THT]"]
  Q5 = Basic FET N-Channel [package="TO220 [THT]"]
  Q6 = Basic FET N-Channel [package="TO220 [THT]"]
  Q7 = Basic FET N-Channel [package="TO220 [THT]"]
  Q8 = Basic FET N-Channel [package="TO220 [THT]"]
  Q9 = Basic FET N-Channel [package="TO220 [THT]"]
  LED2 = Super Flux LED blue [color=Blue]
  LED3 = Super Flux LED blue [color=Green]
  LED4 = Super Flux LED blue [color=Red]
  LED5 = Super Flux LED blue [color=Blue]
  LED6 = Super Flux LED blue [color=Green]
  LED7 = Super Flux LED blue [color=Red]
  RaspberryPi1 = Raspberry Pi Model B
  SONAR1 = Maxbotix MaxSonar Ultrasonic Sensor
  JACK1 = 2.1mm Barrel Jack with Terminal Block
  LCD1 = LCD screen  # not connected
  LCD2 = Adafruit Positive RGB 2x16 LCD  # not connected

nets:
  N1: Q4.gate, RaspberryPi1.#25
  N2: Q4.drain, LED5.anode
  N3: Q4.source, Q5.source, Q6.source, RaspberryPi1.GND, JACK1.NEG
  N4: Q5.gate, RaspberryPi1.#24
  N5: Q5.drain, LED7.anode
  N6: Q6.drain, LED6.anode
  N7: Q7.gate, RaspberryPi1.#21
  N8: Q7.drain, LED3.anode
  N9: Q7.source, Q8.source, Q9.source, RaspberryPi1.SDA
  N10: Q8.gate, RaspberryPi1.#18
  N11: Q8.drain, LED4.anode
  N12: Q9.gate, RaspberryPi1.#23
  N13: Q9.drain, LED2.anode
  N14: LED4.cathode, LED7.cathode, JACK1.POS
  5V: RaspberryPi1.5V, SONAR1.+5V
  N15: RaspberryPi1.#22, SONAR1.PW

notes:
  - option A wire Vin to breadboard (does it support 12v??)
  - option B is external 12v female adapter

custom parts:
  Raspberry Pi Model B: Raspberry Pi (Model B)
  Maxbotix MaxSonar Ultrasonic Sensor: Maxbotix MaxSonar Ultrasonic Sensor LV-EZ0, LV-EZ1, LV-EZ2, LV-EZ3, LV-EZ4
  Adafruit Positive RGB 2x16 LCD: Adafruit Positive 2x16 LCD Display with RGB Backlight
