# Fritzing sketch Arduino+RangeSensor (saved by Fritzing 0.7.11b)

parts:
  Arduino3 = Arduino  # not connected
  SONAR2 = Maxbotix MaxSonar Ultrasonic Sensor
  Part2 = Arduino ProtoShield
  J10 = Generic female header - 3 pins [package=THT]
  J11 = Generic female header - 3 pins [package=THT]

nets:
  N1: SONAR2.GND, J10.pin1
  N2: SONAR2.+5V, J11.pin1
  N3: SONAR2.AN, Part2.A0

notes:
  Maxbotix Range Sensor
  Arduino Protoshield
  N/A
  A0
  5V
  GND

custom parts:
  Maxbotix MaxSonar Ultrasonic Sensor: Maxbotix MaxSonar Ultrasonic Sensor LV-EZ0, LV-EZ1, LV-EZ2, LV-EZ3, LV-EZ4
