# Fritzing sketch LCD+Arduino (saved by Fritzing 0.7.11b)

parts:
  Arduino3 = Arduino  # not connected
  LCD3 = LCD screen
  Part2 = Arduino ProtoShield
  J10 = Generic female header - 3 pins [package=THT]
  R3 = Rotary Potentiometer (Large) [maximum_resistance=100kΩ package=THT]
  J11 = Generic female header - 3 pins [package=THT]

nets:
  N1: LCD3.RS, Part2.D12
  N2: LCD3.E, Part2.D11
  N3: LCD3.DB2, LCD3.DB3, LCD3.DB4, Part2.D5
  N4: LCD3.DB5, Part2.D4
  N5: LCD3.DB6, Part2.D3
  N6: LCD3.DB7, Part2.D2
  N7: LCD3.LED+, J10.pin1
  N8: LCD3.LED-, J11.pin1
  N9: R3.leg1, J11.pin2

notes:
  GND x 2
  5V x 2
  D2
  From LCD
  Arduino Pin
  D3
  D4
  D5
  D11
  D12
