# Fritzing sketch platoon_arduino+RPi (saved by Fritzing 0.7.11b)
breadboards: 1

parts:
  Arduino1 = Arduino
  Q4 = Basic FET N-Channel [package="TO220 [THT]"]
  Q5 = Basic FET N-Channel [package="TO220 [THT]"]
  Q6 = Basic FET N-Channel [package="TO220 [THT]"]
  Q7 = Basic FET N-Channel [package="TO220 [THT]"]
  Q8 = Basic FET N-Channel [package="TO220 [THT]"]
  Q9 = Basic FET N-Channel [package="TO220 [THT]"]
  LED2 = Super Flux LED blue [color=Blue]
  LED3 = Super Flux LED blue [color=Green]
  LED4 = Super Flux LED blue [color=Red]
  LED5 = Super Flux LED blue [color=Blue]
  LED6 = Super Flux LED blue [color=Green]
  LED7 = Super Flux LED blue [color=Red]
  RaspberryPi1 = Raspberry Pi Model B
  SONAR1 = Maxbotix MaxSonar Ultrasonic Sensor
  JACK1 = 2.1mm Barrel Jack with Terminal Block
  LCD1 = LCD screen  # not connected
  LCD2 = Adafruit Positive RGB 2x16 LCD  # not connected

nets:
  GND: Arduino1.GND, SONAR1.GND
  N1: Arduino1.D8, SONAR1.PW
  +5V: Arduino1.+5V, SONAR1.+5V
  N2: Q4.gate, RaspberryPi1.#25
  N3: Q4.drain, LED5.anode
  N4: Q4.source, Q5.source, Q6.source, RaspberryPi1.GND, JACK1.NEG
  N5: Q5.gate, RaspberryPi1.#24
  N6: Q5.drain, LED7.anode
  N7: Q6.drain, LED6.anode
  N8: Q7.gate, RaspberryPi1.#21
  N9: Q7.drain, LED3.anode
  N10: Q7.source, Q8.source, Q9.source
  N11: Q8.gate, RaspberryPi1.#17
  N12: Q8.drain, LED4.anode
  N13: Q9.gate, RaspberryPi1.#22
  N14: Q9.drain, LED2.anode
  N15: LED4.cathode, LED7.cathode, JACK1.POS

notes:
  - option A wire Vin to breadboard (does it support 12v??)
  - option B is external 12v female adapter
  USB

custom parts:
  Raspberry Pi Model B: Raspberry Pi (Model B)
  Maxbotix MaxSonar Ultrasonic Sensor: Maxbotix MaxSonar Ultrasonic Sensor LV-EZ0, LV-EZ1, LV-EZ2, LV-EZ3, LV-EZ4
  Adafruit Positive RGB 2x16 LCD: Adafruit Positive 2x16 LCD Display with RGB Backlight
